# Fritzing sketch Wemos 4 Fach Taster (saved by Fritzing 0.9.3b)
circuit board: 4.4cm x 6.35cm

parts:
  J1 = Camdenboss CTB0158-4 [part_number=CTB0158-4 package=THT]
  WeMos_D1_Mini1 = WeMos D1 Mini
  J3 = Camdenboss CTB0158-4 [part_number=CTB0158-4 package=THT]
  J2 = Camdenboss CTB0158-4 [part_number=CTB0158-4 package=THT]
  R2 = Resistor [tolerance=±5% resistance=10k package=THT]
  R1 = Resistor [tolerance=±5% resistance=10k package=THT]

nets:
  N1: J1.pin1, R2.Pin_1
  GND: J1.pin2, J1.pin4, WeMos_D1_Mini1.G, J3.pin1, J3.pin3, J2.pin2, J2.pin4
  N2: J1.pin3, R1.Pin_0
  N3: WeMos_D1_Mini1.3V3, J3.pin4
  N4: WeMos_D1_Mini1.5V, J3.pin2
  N5: WeMos_D1_Mini1.D1, R2.Pin_0
  N6: WeMos_D1_Mini1.D2, R1.Pin_1
  N7: WeMos_D1_Mini1.D3, J2.pin1
  N8: WeMos_D1_Mini1.D4, J2.pin3

notes:
  D1 G D2 G
  D3 G D4 G
  G +5V G +3.3V
